# Fritzing sketch diagram (saved by Fritzing 1.0.6)
breadboards: 2

parts:
  Componente1 = ADS1115
  Componente2 = TXB0108 8-channel Bi-directional Logic Level Converter
  Componente3 = Voltage Sensor 25V
  R1 = Resistor [tolerance=±5% power=0.25W resistance=220 package=THT]
  Componente4 = DC-DC Power Module (5v)
  esp1 = ESP32 DevKitc V4
  esp2 = ESP32 DevKitc V4
  U2 = POT [knob_status=50% power=0.5W package=pot_alpha_rv16af-20]
  Componente5 = DC-DC Power Module (5v)
  A1 = TJA1050 CAN Module
  A2 = TJA1050 CAN Module

nets:
  VDD: Componente1.VDD, Componente2.VCCB, Componente4.Vin, esp2.5V, A1.Pin_3, A2.Pin_3
  GND: Componente1.GND, Componente1.ADDR, Componente2.GND, Componente3.-, R1.Pin_0, Componente4.GND, esp1.GND#32, esp2.GND#18, A1.Pin_4, A2.Pin_4
  N1: Componente1.SCL, esp2.IO22
  N2: Componente1.SDA, esp2.IO18
  N3: Componente1.A0, Componente3.S, R1.Pin_1
  N4: Componente2.B1, A2.Pin_1
  N5: Componente2.B2, A2.Pin_2
  N6: Componente2.B7, A1.Pin_2
  N7: Componente2.B8, A1.Pin_1
  N8: Componente2.OE, Componente2.VCCA, esp1.3V3
  N9: Componente2.A8, esp2.IO5
  N10: Componente2.A7, esp2.IO4
  N11: Componente2.A2, esp1.IO4
  N12: Componente2.A1, esp1.IO5
  N13: Componente3.GND, U2.S
  N14: Componente3.VCC, Componente3.+, U2.E, Componente5.GND*
  N15: U2.A, Componente5.Vout
  N16: A1.Pin_5, A2.Pin_5
  N17: A1.Pin_6, A2.Pin_6

notes:
  Modulo CanBus TJA1050
  Funciona a 10v
  Fuente

custom parts:
  ADS1115: ADC ADS1115
  TXB0108 8-channel Bi-directional Logic Level Converter: Because the Arduino (and Basic Stamp) are 5V devices, and most modern sensors, displays, flash cards and modes are 3.3V-only, many makers find that they need to perform level shifting/conversion to protect the 3.3V device from 5V. Although one can use resistors to make a divider, for high speed transfers, the resistors can add a lot of slew and cause havoc that is tough to debug. For that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
  DC-DC Power Module (5v): DC-DC Power Module based con AMS1117-5.0 Input: DC 6~12V (input power must higher 1V than output power); Output: 5V (+/-0.05V error), 800mA
  ESP32 DevKitc V4: ESP32-DevKitC board with ESP32-WROOM-32 module. ESP32-DevKitC V4 is a small-sized ESP32-based development board produced by Espressif. Most of the pins on the ESP module are broken out to the pin headers on the board. The pins D0, D1, D2, D3, CMD and CLK are used internally for communication between ESP32 and SPI flash memory. They are grouped on both sides near the USB connector. Avoid using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
  TJA1050 CAN Module: TJA1050 CAN module CAN bus module.
