# Fritzing sketch diagram (saved by Fritzing 1.0.5)
breadboards: 2

parts:
  Componente1 = Adafruit ADS1115 16Bit I2C ADC [part_number="Adafruit #1085"]
  esp1 = ESP32 DevKitc V4
  Mod1 = Voltage Sensor 25V
  R1 = Resistor [tolerance=±5% resistance=1k package="2010 [SMD]"]
  A1 = MAX6675 module [package=THT]
  A2 = MAX6675 module [package=THT]
  A3 = MAX6675 module [package=THT]
  A4 = MAX6675 module [package=THT]
  A5 = MAX6675 module [package=THT]
  A6 = MAX6675 module [package=THT]

nets (from the schematic view):
  N1: Componente1.AIN0, Mod1.S, R1.Pin_1
  N2: Componente1.ADDR, Componente1.GND, esp1.GND#12, Mod1.-, R1.Pin_0, A1.pin1, A2.pin1, A3.pin1, A4.pin1, A5.pin1, A6.pin1
  N3: Componente1.SDA, esp1.IO22
  N4: Componente1.SCL, esp1.IO21
  VDD: Componente1.VDD, esp1.5V, A1.pin2, A2.pin2, A3.pin2, A4.pin2, A5.pin2, A6.pin2
  N5: esp1.IO15, A4.pin4
  N6: esp1.IO2, A5.pin4
  N7: esp1.IO4, A6.pin4
  N8: esp1.IO16, A3.pin4
  N9: esp1.IO17, A2.pin4
  N10: esp1.IO5, A1.pin4
  N11: esp1.IO18, A1.pin3, A2.pin3, A3.pin3, A4.pin3, A5.pin3, A6.pin3
  N12: esp1.IO19, A1.pin5, A2.pin5, A3.pin5, A4.pin5, A5.pin5, A6.pin5

custom parts:
  Adafruit ADS1115 16Bit I2C ADC: For microcontrollers without an analog-to-digital converter or when you want a higher-precision ADC, the ADS1115 provides 16-bit precision at 860 samples/second over I2C. The chip can be configured as 4 single-ended input channels, or two differential channels. As a nice bonus, it even includes a programmable gain amplifier, up to x16, to help boost up smaller single/differential signals to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
  ESP32 DevKitc V4: ESP32-DevKitC board with ESP32-WROOM-32 module. ESP32-DevKitC V4 is a small-sized ESP32-based development board produced by Espressif. Most of the pins on the ESP module are broken out to the pin headers on the board. The pins D0, D1, D2, D3, CMD and CLK are used internally for communication between ESP32 and SPI flash memory. They are grouped on both sides near the USB connector. Avoid using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
  MAX6675 module: MAX6675 Module + K Type Thermocouple Sensor Temperature Degrees.
